# Fritzing sketch schema (saved by Fritzing 0.9.10b)
breadboards: 1

parts:
  S1 = Pushbutton [package="[THT]"]
  R1 = Photocell (LDR) [package=THT]
  R2 = Resistor [tolerance=±5% resistance=220 package="2512 [SMD]"]
  R3 = Resistor [tolerance=±5% resistance=220 package="2512 [SMD]"]
  Display1 = LCD screen 16x2 IIC [part_number=101290]
  M1 = BME680 Module [part_number=CJMCU-680]
  U1 = ESP32S-HiLetgo [part_number=ESP32S-HiLetgo]
  J1 = Basic Servo

nets:
  N1: S1.Pin_1, S1.Pin_2, R3.Pin_0, U1.GPIO33
  GND: S1.Pin_3, S1.Pin_4, R1.pin_0, R2.Pin_1, R3.Pin_1, Display1.GND, M1.GND, M1.SCL, U1.GND, J1.gnd
  N2: R1.pin_1, R2.Pin_0, U1.EN
  VCC: Display1.VCC, M1.VCC, U1.3.3, J1.vcc
  N3: Display1.SDA, U1.GPIO21
  N4: Display1.SCL, U1.GPIO22
  N5: M1.SDA, U1.GPIO23
  N6: M1.SDO, U1.GPIO19
  N7: M1.CS, U1.GPIO5
  N8: U1.GPIO4, J1.pulse

custom parts:
  LCD screen 16x2 IIC: LCD screen with HD44780 controller enables showing text, symbols, value or anything else that comes from Croduino/Arduino. It is capable of showing 16 symbols in two lines and therefore can be used in many projects that need to send clearly visible and legible output information.. • Color of symbols: White • Backlight: Blue • Dimensions: 80 x 36 x 12 mm • Screen dimensions: 64.5 x 16 mm •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
  BME680 Module: Bosch BME680 Development Module The BME680 is a digital 4-in-1 sensor that measures air quality [gas], humidity, pressure and temperature. Links: BME680 product datasheet
  ESP32S-HiLetgo: HiLetgo ESP-WROOM-32 ESP32 ESP-32S Development Board 2.4GHz Dual-Mode WiFi + Bluetooth Dual Cores Microcontroller The ESP32 integrated with Antenna switches, RF Balun, power amplifiers, low-noise amplifiers, filters, and management modules, and the entire solution occupies the least area of PCB. 2.4 GHz Wi-Fi plus Bluetooth dual-mode chip, with TSMC Ultra-low power consumption 40nm technology,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
